// Logisim project game.circ as structural Verilog: 14 circuits, main circuit mainCPU
module Computer (
);

  wire and_1_out, button_2_out, button_3_out, button_4_out, button_5_out, ck, en, gpu_1_p10, gpu_1_p11,
       gpu_1_p12, myCPU_next, myCPU_r_w, not_1_out, or_1_out, port_range_1_select, port_s_1_write_enable,
       port_s_3_write_enable, port_s_4_write_enable, port_sel_1_ram_sel, red_or_1_p1, red_or_1_p4,
       red_or_1_p7, rt;
  wire [0:0] gpu_1_p6;
  wire [1:0] myCPU_phase;
  wire [7:0] Apple_Coordinate_out, ck_counter_q, Control_Vector_q, controlled_buffer_1_out,
       controlled_buffer_5_out, Cover_if_q, cycle_counter_q, myCPU_address_bus, myCPU_dataout, myCPU_out_9,
       myCPU_out_10, myCPU_out_11, myCPU_out_12;
  wire [15:0] counter_1_q;

  Clock #(.highDuration(1), .lowDuration(1)) clock_1 (.out(ck));
  Button button_1 (.out(rt));
  Counter #(.width(8), .max('hff), .ongoal("wrap"), .trigger("rising"), .behavior("old")) ck_counter (
    .Q(ck_counter_q), .clk(ck), .clr(rt));  // open: load, D, count, carry, preset
  // Probe on ck_counter_q
  Button button_2 (.out(button_2_out));
  Button button_3 (.out(button_3_out));
  Button button_4 (.out(button_4_out));
  assign controlled_buffer_1_out = button_3_out ? 8'h10 : 8'bz;  // Controlled_Buffer controlled_buffer_1
  Counter #(.width(8), .max('hff), .ongoal("wrap"), .trigger("rising"), .behavior("old")) cycle_counter (
    .count(myCPU_next), .Q(cycle_counter_q), .clk(ck), .clr(rt));  // open: load, D, carry, preset
  // Probe on cycle_counter_q
  // Probe on myCPU_phase
  Button button_5 (.out(button_5_out));
  assign controlled_buffer_1_out = button_2_out ? {8{1'b1}} : 8'bz;  // Controlled_Buffer controlled_buffer_2
  assign controlled_buffer_1_out = button_4_out ? 8'h1 : 8'bz;  // Controlled_Buffer controlled_buffer_3
  assign controlled_buffer_1_out = button_5_out ? 8'hf0 : 8'bz;  // Controlled_Buffer controlled_buffer_4
  // Probe on myCPU_out_9
  // Probe on myCPU_out_10
  mainCPU myCPU (
    .CK(ck), .RT(rt), .Datain(controlled_buffer_5_out), .address_bus(myCPU_address_bus),
    .Dataout(myCPU_dataout), .R_W(myCPU_r_w), .Phase(myCPU_phase), .next(myCPU_next), .out_9(myCPU_out_9),
    .out_10(myCPU_out_10), .out_11(myCPU_out_11), .out_12(myCPU_out_12));  // open: IRQ
  // Probe on myCPU_out_11
  // Probe on myCPU_out_12
  assign controlled_buffer_5_out = port_s_1_write_enable ? Apple_Coordinate_out : 8'bz;  // Controlled_Buffer controlled_buffer_5
  Random #(.width(8), .seed(0), .trigger("rising")) Apple_Coordinate (
    .clk(en), .next(en), .out(Apple_Coordinate_out));  // open: clr
  Port_S port_s_1 (.Write_Enable(port_s_1_write_enable), .Address_Bus(myCPU_address_bus), .Port_s_Address(8'hfd));
  Port_S port_s_2 (.Write_Enable(en), .Address_Bus(myCPU_address_bus), .Port_s_Address(8'hfe));
  Register #(.width(8), .trigger("rising"), .Select("low")) Control_Vector (
    .D(controlled_buffer_1_out), .Q(Control_Vector_q), .clk(or_1_out));  // open: en, clr
  assign controlled_buffer_5_out = port_s_3_write_enable ? Control_Vector_q : 8'bz;  // Controlled_Buffer controlled_buffer_6
  Port_S port_s_3 (.Write_Enable(port_s_3_write_enable), .Address_Bus(myCPU_address_bus), .Port_s_Address(8'hfc));
  or or_1 (or_1_out, button_5_out, button_2_out, button_4_out, button_3_out);
  assign controlled_buffer_5_out = port_s_4_write_enable ? Cover_if_q : 8'bz;  // Controlled_Buffer controlled_buffer_7
  Port_S port_s_4 (.Write_Enable(port_s_4_write_enable), .Address_Bus(myCPU_address_bus), .Port_s_Address({8{1'b1}}));
  and and_1 (and_1_out, myCPU_r_w, port_range_1_select);
  Port_range port_range_1 (
    .Select(port_range_1_select), .Address_Bus(myCPU_address_bus), .Range_LOW(8'he0), .Range_HIGH(8'he1));
  Port_Sel port_sel_1 (.Addr(myCPU_address_bus), .RAM_sel(port_sel_1_ram_sel));  // open: IO_sel
  Register #(.width(8), .trigger("rising"), .Select("low")) Cover_if (
    .D({{7{1'b0}}, gpu_1_p6[0]}), .en(and_1_out), .Q(Cover_if_q), .clk(ck), .clr(rt));
  // GPU gpu_1: pin names not known; wires that end beside it: myCPU_r_w, myCPU_dataout, myCPU_address_bus, controlled_buffer_5_out, myCPU_dataout, gpu_1_p6[0], 1'b1, myCPU_address_bus[0], 1'b1, gpu_1_p10, gpu_1_p11, gpu_1_p12, gpu_1_p10, gpu_1_p11, gpu_1_p12, and_1_out, ck, rt
  RAM #(.addrWidth(8), .dataWidth(8), .bus("separate"), .Select("high")) ram_1 (
    .addr(myCPU_address_bus), .din(myCPU_dataout), .data(controlled_buffer_5_out), .str(myCPU_r_w),
    .sel(port_sel_1_ram_sel), .clk(ck), .ld(not_1_out));  // open: clr
  // Probe on controlled_buffer_5_out
  not not_1 (not_1_out, myCPU_r_w);
  // _16_16_frame_buffer 16_16_frame_buffer_1: pin names not known; wires that end beside it: Apple_Coordinate_out
  DotMatrix #(.inputtype("row"), .matrixcols(16), .matrixrows(16), .persist(0), .dotshape("square")) dotmatrix_1 ();  // open: row0, row1, row2, row3, row4, row5, row6, row7, row8, row9, row10, row11, row12, row13, row14, row15
  // red_OR red_or_1: pin names not known; wires that end beside it: red_or_1_p1, red_or_1_p1, myCPU_r_w, red_or_1_p4, red_or_1_p4, red_or_1_p4, red_or_1_p7, red_or_1_p7
  // Probe on controlled_buffer_5_out
  // Probe on myCPU_address_bus
  // Probe on myCPU_dataout
  // Probe on counter_1_q
  Counter #(.width(16), .max('hffff), .ongoal("wrap"), .trigger("rising"), .behavior("new")) counter_1 (
    .count(en), .Q(counter_1_q), .clk(ck), .clr(rt));  // open: load, D, carry, preset, down

  // Notes on the sheet:
  //   2025.06.10 Snack optimized
  //   2025.06.22 Snack finalized
  //   CLOCK
  //   DATA_IN BUS
  //   ADDRESS BUS
  //   DATA_OUT BUS
  //   Control_read/write
endmodule

module mainCPU (
  input  CK,
  input  RT,
  input  [7:0] Datain,
  input  [3:0] IRQ,
  output R_W,
  output [1:0] Phase,
  output next,
  output [7:0] address_bus,
  output [7:0] out_9,
  output [7:0] out_10,
  output [7:0] out_11,
  output [7:0] out_12,
  output [7:0] Dataout
);

  wire _0, button_1_out, ck_t, cu_fsm_1_nobranch_pc_2, cu_fsm_1_syscall, hlt, imload, imsel, inta, IRld,
       IRsel, it, not_1_out, or_1_out, pcload, pull_resistor_2_node, ret, RFwrite, tunnel, tunnel_t, undriven;
  wire [1:0] addrsel, ivt, multiplexer_4_out, pcsel, RFsel;
  wire [7:0] alu_1_result, controlled_buffer_2_out, multiplexer_2_out, op, pc_1_pc_1, pc_1_pc_out,
       ram_1_data, register_1_q, register_2_q, rf_1_dbus, rf_1_sbus, sp_1_out_6, undriven_2, undriven_3;

  LED #(.active("true")) Tik_Tok (.in(or_1_out));
  LED #(.active("true")) Halt (.in(hlt));
  Button button_1 (.out(button_1_out));
  Pull_Resistor #(.pull(0)) pull_resistor_1 (.node(hlt));
  or or_1 (or_1_out, button_1_out, it, ~hlt);  // OR_Gate
  assign ck_t = or_1_out ? CK : 1'bz;  // Controlled_Buffer controlled_buffer_1
  Register #(.width(8), .trigger("rising"), .Select("low")) register_1 (
    .D(Datain), .en(IRld), .Q(register_1_q), .clk(ck_t), .clr(RT));
  Register #(.width(8), .trigger("rising"), .Select("low")) register_2 (
    .D(Datain), .en(imload), .Q(register_2_q), .clk(ck_t));  // open: clr
  // Probe on Datain
  Multiplexer #(.select(1), .width(8), .disabled(0), .enable("false")) multiplexer_1 (
    .in0(Datain), .in1(register_1_q), .out(op), .sel(pull_resistor_2_node));
  Pull_Resistor #(.pull(0)) pull_resistor_2 (.node(pull_resistor_2_node));
  Multiplexer #(.select(2), .width(8), .disabled("Z"), .enable("false")) multiplexer_2 (
    .in0(alu_1_result), .in1(controlled_buffer_2_out), .in2(Datain), .in3(pc_1_pc_1),
    .out(multiplexer_2_out), .sel(RFsel));
  // Probe on op
  assign controlled_buffer_2_out = ~tunnel_t ? rf_1_sbus : 8'bz;  // Controlled_Buffer controlled_buffer_2
  assign controlled_buffer_2_out = tunnel_t ? ~rf_1_sbus : 8'bz;  // Controlled_Inverter controlled_inverter_1
  RF rf_1 (
    .dbus(rf_1_dbus), .sbus(rf_1_sbus), .dregsel(op[1:0]), .sregsel(op[3:2]), .dval(multiplexer_2_out),
    .dwrite(RFwrite), .r0(out_9), .r1(out_10), .r2(out_11), .r3(out_12), .Zero(_0), .Negative(tunnel),
    .in_5(RT), .in_4(ck_t));
  // Probe on multiplexer_2_out
  PC pc_1 (
    .Imme(Datain), .rs(rf_1_sbus), .pc_1(pc_1_pc_1), .PC_out(pc_1_pc_out), .inta(inta), .pcsel(pcsel),
    .pcload(pcload), .nobranch(cu_fsm_1_nobranch_pc_2), .IVT(ivt), .ck(ck_t), .rt(RT), .intr(it),
    .next(next), .\return (undriven), .syscall(cu_fsm_1_syscall));
  PIC pic_1 (.IRQ(IRQ), .IVT(ivt), .interupt_IRQ(it), .inta(inta), .RT(RT), .\return (ret));
  CU_FSM cu_fsm_1 (
    .\μops ({next, imload, imsel, pcload, pcsel, addrsel, R_W, IRsel, IRld, RFwrite, RFsel}),
    .nobranch_PC_2(cu_fsm_1_nobranch_pc_2), .Opcode(op), .Z(_0), .N(tunnel), .CP(ck_t), .phase(Phase),
    .RT(RT), .ret_back(ret), .halt(hlt), .syscall(cu_fsm_1_syscall));
  // Probe on pc_1_pc_out
  SP sp_1 (.out_6(sp_1_out_6), .Opcode(op), .cp(ck_t), .rt(RT), .IVT(ivt), .next(next));
  or or_2 (pull_resistor_2_node, Phase[1], Phase[0]);
  Multiplexer #(.select(2), .width(8), .disabled("Z"), .enable("false")) multiplexer_3 (
    .in0(pc_1_pc_out), .in1(register_2_q), .in2(rf_1_sbus), .in3(sp_1_out_6), .out(address_bus),
    .sel(multiplexer_4_out));
  Multiplexer #(.select(1), .width(2), .disabled(0), .enable("false")) multiplexer_4 (
    .in0(2'b00), .in1(addrsel), .out(multiplexer_4_out), .sel(pull_resistor_2_node));
  ALU alu_1 (
    .A_rd(rf_1_dbus), .Result(alu_1_result), .B_rs(rf_1_sbus), .Opcode(op), .rs__rd(tunnel_t));  // open: Zero, Negative
  // Probe on {next, imload, imsel, pcload, pcsel, addrsel, R_W, IRsel, IRld, RFwrite, RFsel}
  assign Dataout = R_W ? rf_1_dbus : 8'bz;  // Controlled_Buffer controlled_buffer_3
  not not_1 (not_1_out, R_W);
  RAM #(.addrWidth(8), .dataWidth(8), .bus("separate"), .Select("high")) ram_1 (
    .addr(undriven_2), .din(undriven_3), .data(ram_1_data), .str(R_W), .clk(ck_t), .ld(not_1_out));  // open: sel, clr

  // Other names for the same wires on the sheet: rd[1:0] = op[1:0]; rs[1:0] = op[3:2]

  // Notes on the sheet:
  //   Clock Pulse
  //   IR
  //   Immed
  //   Regs
  //   8-bit Multicycle CPU
  //   dataout bus
  //   if rs==rd
endmodule

module PC (
  input  [1:0] pcsel,
  input  pcload,
  input  nobranch,
  input  \return ,
  input  [7:0] Imme,
  input  [7:0] rs,
  input  ck,
  input  rt,
  input  [1:0] IVT,
  input  next,
  input  syscall,
  input  intr,
  output [7:0] pc_1,
  output [7:0] PC_out,
  output inta
);

  wire and_1_out, and_2_out, not_1_out, or_1_out;
  wire [1:0] multiplexer_3_out;
  wire [7:0] BL_q, multiplexer_1_out, multiplexer_2_out, multiplexer_4_out, multiplexer_5_out;

  Multiplexer #(.select(2), .width(8), .disabled("Z"), .enable("false")) multiplexer_1 (
    .in0(pc_1), .in1(Imme), .in2(rs), .in3(BL_q), .out(multiplexer_1_out), .sel(pcsel));
  Multiplexer #(.select(2), .width(8), .disabled("Z"), .enable("false")) multiplexer_2 (
    .in0(8'hc0), .in1(8'hd0), .in2(8'he0), .in3(8'hf0), .out(multiplexer_2_out), .sel(multiplexer_3_out));
  Multiplexer #(.select(1), .width(2), .disabled("Z"), .enable("false")) multiplexer_3 (
    .in0(IVT), .in1(Imme[1:0]), .out(multiplexer_3_out), .sel(syscall));
  Register #(.width(8), .trigger("rising"), .Select("low")) BL (
    .D(multiplexer_1_out), .en(and_1_out), .Q(BL_q), .clk(ck), .clr(rt));
  Multiplexer #(.select(1), .width(8), .disabled("Z"), .enable("false")) multiplexer_4 (
    .in0(multiplexer_1_out), .in1(multiplexer_2_out), .out(multiplexer_4_out), .sel(and_1_out));
  Register #(.width(8), .trigger("rising"), .Select("low")) register_1 (
    .D(multiplexer_4_out), .en(pcload), .Q(PC_out), .clk(ck), .clr(rt));
  and and_1 (and_1_out, or_1_out, next);
  or or_1 (or_1_out, syscall, intr);
  Pull_Resistor #(.pull(0)) pull_resistor_1 (.node(intr));
  Multiplexer #(.select(1), .width(8), .disabled("Z"), .enable("false")) multiplexer_5 (
    .in0(8'h1), .in1(8'h2), .out(multiplexer_5_out), .sel(nobranch));
  Adder #(.width(8)) adder_1 (.a(multiplexer_5_out), .b(PC_out), .out(pc_1));  // open: cin, cout
  and and_2 (and_2_out, ck, not_1_out);
  not not_1 (not_1_out, ck);
  and and_3 (inta, and_1_out, and_2_out);

  // Notes on the sheet:
  //   中断向量
  //   next PC
  //   PC
  //   PC+1
  //   中断响应
endmodule

module SP (
  input  [7:0] Opcode,
  input  next,
  input  cp,
  input  rt,
  input  [1:0] IVT,
  output [7:0] out_6
);

  wire and_1_out, and_2_out, comparator_1_eq;
  wire [7:0] adder_1_out, multiplexer_1_out, multiplexer_2_out, multiplexer_3_out, register_1_q,
       subtractor_1_out;

  Comparator #(.width(5), .mode("unsigned")) comparator_1 (
    .a(Opcode[7:3]), .b(5'b10110), .eq(comparator_1_eq));  // open: gt, lt
  and and_1 (and_1_out, comparator_1_eq, next);
  // Probe on and_1_out
  Adder #(.width(8)) adder_1 (.a(register_1_q), .b(8'h1), .out(adder_1_out));  // open: cin, cout
  Multiplexer #(.select(1), .width(8), .disabled("Z"), .enable("false")) multiplexer_1 (
    .in0(adder_1_out), .in1(subtractor_1_out), .out(multiplexer_1_out), .sel(and_2_out));
  Subtractor #(.width(8)) subtractor_1 (.a(register_1_q), .b(8'h1), .out(subtractor_1_out));  // open: bin, bout
  and and_2 (and_2_out, Opcode[2], comparator_1_eq);
  // Probe on and_2_out
  Register #(.width(8), .trigger("rising"), .Select("low")) register_1 (
    .D(multiplexer_1_out), .en(and_1_out), .Q(register_1_q), .clk(cp), .clr(rt));
  Multiplexer #(.select(1), .width(8), .disabled("Z"), .enable("false")) multiplexer_2 (
    .in0(register_1_q), .in1(subtractor_1_out), .out(multiplexer_2_out), .sel(and_2_out));
  Adder #(.width(8)) adder_2 (.a(multiplexer_2_out), .b(multiplexer_3_out), .out(out_6));  // open: cin, cout
  Multiplexer #(.select(2), .width(8), .disabled("Z"), .enable("false")) multiplexer_3 (
    .in0(8'hb0), .in1(8'hb4), .in2(8'hb8), .in3(8'hbc), .out(multiplexer_3_out), .sel(IVT));

  // Notes on the sheet:
  //   en~+/-
  //   0-0 null
  //   1-0 push
  //   1-1 pop
  //   2025.05.11
  //   0-1 read out
endmodule

module PIC (
  input  [3:0] IRQ,
  input  inta,
  input  \return ,
  input  RT,
  output [1:0] IVT,
  output interupt_IRQ
);

  wire d_ff_2_q, or_1_out, or_2_out, priority_encoder_1_gs;
  wire [1:0] priority_encoder_1_out;
  wire [7:0] multiplexer_1_out;

  Priority_Encoder #(.select(2), .disabled("Z")) priority_encoder_1 (
    .in0(IRQ[0]), .in1(IRQ[1]), .in2(IRQ[2]), .in3(IRQ[3]), .out(priority_encoder_1_out),
    .gs(priority_encoder_1_gs));  // open: en_out, en_in
  Register #(.width(2), .trigger("rising"), .Select("low")) register_1 (
    .D(priority_encoder_1_out), .Q(IVT), .clk(priority_encoder_1_gs), .clr(or_2_out));  // open: en
  D_Flip_Flop #(.trigger("rising"), .Pre_Clr_Positions("LEGACY"), .NegatePresetClear("false"), .enable("true"), .NewFFLayout("false")) d_ff_1 (
    .clk(priority_encoder_1_gs), .D(1'b1), .Q(interupt_IRQ), .reset(or_1_out));  // open: Qn, preset, en
  or or_1 (or_1_out, d_ff_2_q, RT);
  D_Flip_Flop #(.trigger("rising"), .Pre_Clr_Positions("LEGACY"), .NegatePresetClear("false"), .enable("true"), .NewFFLayout("false")) d_ff_2 (
    .Q(d_ff_2_q), .preset(inta), .reset(or_2_out));  // open: clk, D, Qn, en
  Multiplexer #(.select(2), .width(8), .disabled("Z"), .enable("false")) multiplexer_1 (
    .in0(8'hc0), .out(multiplexer_1_out), .sel(IVT));  // open: in1, in2, in3
  or or_2 (or_2_out, RT, \return );

  // Notes on the sheet:
  //   中断向量
  //   中断触发
  //   中断响应
endmodule

module CU_FSM (
  input  CP,
  input  RT,
  input  [7:0] Opcode,
  input  Z,
  input  N,
  output [13:0] \μops ,
  output [1:0] phase,
  output nobranch_PC_2,
  output syscall,
  output ret_back,
  output halt
);

  wire _0, and_1_out, and_2_out, and_3_out, comparator_4_eq, not_1_out, or_1_out, or_2_out;
  wire [3:0] and_5_out, decoder_1_out0;
  wire [3:3] not_3_out;
  wire [13:0] multiplexer_1_out, multiplexer_2_out, multiplexer_3_out, multiplexer_4_out, multiplexer_5_out,
       multiplexer_6_out, multiplexer_7_out, multiplexer_8_out, multiplexer_9_out, multiplexer_10_out,
       multiplexer_11_out, multiplexer_12_out, multiplexer_13_out, multiplexer_14_out, multiplexer_15_out,
       multiplexer_16_out;

  Multiplexer #(.select(1), .width(14), .disabled("Z"), .enable("false")) multiplexer_1 (
    .in0(14'h408), .in1(14'h2510), .out(multiplexer_1_out), .sel(phase[0]));
  Multiplexer #(.select(2), .width(14), .disabled("Z"), .enable("false")) multiplexer_2 (
    .in0(14'h408), .in1(14'h1017), .in2(14'hc70), .in3(14'h2510), .out(multiplexer_2_out), .sel(phase));
  Multiplexer #(.select(4), .width(14), .disabled("Z"), .enable("false")) multiplexer_3 (
    .in0(14'h2400), .in1(14'h2400), .in2(14'h2400), .in3(14'h2400), .in4(multiplexer_2_out),
    .in5(multiplexer_1_out), .in8(14'h2700), .in9(14'h2400), .in10(14'h2400), .in11(14'h2400),
    .in12(14'h2400), .in13(14'h2400), .in14(14'h2400), .in15(14'h2400), .out(multiplexer_3_out),
    .sel(Opcode[3:0]));  // open: in6, in7
  Multiplexer #(.select(1), .width(14), .disabled("Z"), .enable("false")) multiplexer_4 (
    .in0(14'h8), .in1(14'h24f0), .out(multiplexer_4_out), .sel(phase[0]));
  Multiplexer #(.select(1), .width(14), .disabled("Z"), .enable("false")) multiplexer_5 (
    .in0(14'h8), .in1(14'h24d6), .out(multiplexer_5_out), .sel(phase[0]));
  Counter #(.width(2), .max('h3), .ongoal("wrap"), .trigger("rising"), .behavior("old")) u_Phase (
    .Q(phase), .clk(and_1_out), .clr(or_1_out));  // open: load, D, count, carry, preset
  and and_1 (and_1_out, and_3_out, ~\μops [13]);  // AND_Gate
  and and_2 (and_2_out, and_3_out, \μops [13]);
  and and_3 (and_3_out, CP, not_1_out);
  not not_1 (not_1_out, CP);
  Multiplexer #(.select(1), .width(14), .disabled("Z"), .enable("false")) multiplexer_6 (
    .in0(14'h408), .in1(14'h2517), .out(multiplexer_6_out), .sel(phase[0]));
  Multiplexer #(.select(2), .width(14), .disabled("Z"), .enable("false")) multiplexer_7 (
    .in0(multiplexer_4_out), .in1(multiplexer_5_out), .in2(14'h2404), .in3(14'h2400),
    .out(multiplexer_7_out), .sel(Opcode[3:2]));
  Multiplexer #(.select(2), .width(14), .disabled("Z"), .enable("false")) multiplexer_8 (
    .in0(14'h408), .in1(14'h1010), .in2(14'h2c56), .out(multiplexer_8_out), .sel(phase));  // open: in3
  Multiplexer #(.select(2), .width(14), .disabled("Z"), .enable("false")) multiplexer_9 (
    .in0(14'h408), .in1(14'h1010), .in2(14'h2c70), .out(multiplexer_9_out), .sel(phase));  // open: in3
  or or_1 (or_1_out, and_2_out, RT);
  Comparator #(.width(8), .mode("twosComplement")) comparator_1 (.a(Opcode), .b(8'hf8), .eq(ret_back));  // open: gt, lt
  Comparator #(.width(6), .mode("twosComplement")) comparator_2 (
    .a(Opcode[7:2]), .b(6'b111100), .eq(syscall));  // open: gt, lt
  Comparator #(.width(8), .mode("twosComplement")) comparator_3 (.a(Opcode), .b({8{1'b1}}), .eq(halt));  // open: gt, lt
  Multiplexer #(.select(1), .width(14), .disabled("Z"), .enable("false")) multiplexer_10 (
    .in0(14'h2400), .in1(14'h2600), .out(multiplexer_10_out), .sel(or_2_out));
  Multiplexer #(.select(1), .width(14), .disabled("Z"), .enable("false")) multiplexer_11 (
    .in0(14'h8), .in1(14'h2496), .out(multiplexer_11_out), .sel(phase[0]));
  Multiplexer #(.select(1), .width(14), .disabled("Z"), .enable("false")) multiplexer_12 (
    .in0(14'h8), .in1(14'h24b0), .out(multiplexer_12_out), .sel(phase[0]));
  Multiplexer #(.select(1), .width(14), .disabled("Z"), .enable("false")) multiplexer_13 (
    .in0(14'h408), .in1(14'h2416), .out(multiplexer_13_out), .sel(phase[0]));
  Multiplexer #(.select(2), .width(14), .disabled("Z"), .enable("false")) multiplexer_14 (
    .in0(multiplexer_13_out), .in1(multiplexer_8_out), .in2(multiplexer_9_out), .in3(multiplexer_6_out),
    .out(multiplexer_14_out), .sel(Opcode[3:2]));
  Multiplexer #(.select(1), .width(14), .disabled("Z"), .enable("false")) multiplexer_15 (
    .in0(14'h2400), .in1(multiplexer_16_out), .out(multiplexer_15_out), .sel(or_2_out));
  Multiplexer #(.select(1), .width(14), .disabled("Z"), .enable("false")) multiplexer_16 (
    .in0(14'h408), .in1(14'h2510), .out(multiplexer_16_out), .sel(phase[0]));
  Multiplexer #(.select(4), .width(14), .disabled("Z"), .enable("false")) multiplexer_17 (
    .in0(14'h2404), .in1(14'h2404), .in2(14'h2404), .in3(14'h2404), .in4(14'h2404), .in5(14'h2404),
    .in6(14'h2404), .in7(14'h2404), .in8(14'h2405), .in9(multiplexer_11_out), .in10(multiplexer_12_out),
    .in11(multiplexer_7_out), .in12(multiplexer_10_out), .in13(multiplexer_14_out),
    .in14(multiplexer_15_out), .in15(multiplexer_3_out), .out(\μops ), .sel(Opcode[7:4]));
  // Probe on Opcode[6:4]
  Comparator #(.width(4), .mode("twosComplement")) comparator_4 (
    .a(4'b1110), .b(Opcode[7:4]), .eq(comparator_4_eq));  // open: gt, lt
  Decoder #(.select(2), .tristate("false"), .disabled(0), .enable("true")) decoder_1 (
    .out0(decoder_1_out0[0]), .out1(decoder_1_out0[1]), .out2(decoder_1_out0[2]), .out3(decoder_1_out0[3]),
    .sel(Opcode[3:2]), .en(comparator_4_eq));
  and and_4 (nobranch_PC_2, comparator_4_eq, ~or_2_out);  // AND_Gate
  or or_2 (or_2_out, and_5_out[3], and_5_out[2], and_5_out[1], and_5_out[0]);
  assign and_5_out = decoder_1_out0 & {not_3_out[3], N, Z, _0};  // AND_Gate and_5, 4 bits wide
  not not_2 (_0, Z);
  not not_3 (not_3_out[3], N);

  // Other names for the same wires on the sheet: p[1:0] = phase

  // Notes on the sheet:
  //   branch
  //   Branch
endmodule

module RF (
  input  dwrite,
  input  [1:0] dregsel,
  input  [7:0] dval,
  input  in_4,
  input  in_5,
  input  [1:0] sregsel,
  output [7:0] r0,
  output [7:0] dbus,
  output [7:0] r1,
  output Zero,
  output [7:0] r2,
  output Negative,
  output [7:0] r3,
  output [7:0] sbus
);

  wire demultiplexer_1_out0, demultiplexer_1_out1, demultiplexer_1_out2, demultiplexer_1_out3, or_1_out;

  Demultiplexer #(.select(2), .width(1), .tristate("false"), .disabled("Z"), .enable("false")) demultiplexer_1 (
    .out0(demultiplexer_1_out0), .out1(demultiplexer_1_out1), .out2(demultiplexer_1_out2),
    .out3(demultiplexer_1_out3), .in(dwrite), .sel(dregsel));
  Register #(.width(8), .trigger("rising"), .Select("low")) register_1 (
    .D(dval), .en(demultiplexer_1_out0), .Q(r0), .clk(in_4), .clr(in_5));
  Register #(.width(8), .trigger("rising"), .Select("low")) register_2 (
    .D(dval), .en(demultiplexer_1_out1), .Q(r1), .clk(in_4), .clr(in_5), .preset(in_5));  // open: cs
  Register #(.width(8), .trigger("rising"), .Select("low")) register_3 (
    .D(dval), .en(demultiplexer_1_out2), .Q(r2), .clk(in_4), .clr(in_5), .preset(in_5));  // open: cs
  Register #(.width(8), .trigger("rising"), .Select("low")) register_4 (
    .D(dval), .en(demultiplexer_1_out3), .Q(r3), .clk(in_4), .clr(in_5), .preset(in_5));  // open: cs
  Multiplexer #(.select(2), .width(8), .disabled("Z"), .enable("false")) multiplexer_1 (
    .in0(r0), .in1(r1), .in2(r2), .in3(r3), .out(dbus), .sel(dregsel));
  Multiplexer #(.select(2), .width(8), .disabled("Z"), .enable("false")) multiplexer_2 (
    .in0(r0), .in1(r1), .in2(r2), .in3(r3), .out(sbus), .sel(sregsel));
  or or_1 (or_1_out, dbus[0], dbus[1], dbus[2], dbus[3], dbus[4], dbus[5], dbus[6], dbus[7]);
  not not_1 (Zero, or_1_out);

  assign Negative = dbus[7];

  // Notes on the sheet:
  //   Register File
endmodule

module ALU (
  input  [7:0] Opcode,
  input  [7:0] B_rs,
  input  [7:0] A_rd,
  output rs__rd,
  output [7:0] Result,
  output Zero,
  output Negative
);

  wire or_2_out;
  wire [7:0] adder_1_out, adder_2_out, alu_1_out, and_1_out, divider_1_out, multiplexer_1_out,
       multiplexer_2_out, multiplier_1_out, or_1_out, subtractor_1_out, xor_1_out;

  Multiplexer #(.select(1), .width(8), .disabled("Z"), .enable("false")) multiplexer_1 (
    .in0(B_rs), .in1(8'h1), .out(multiplexer_1_out), .sel(rs__rd));
  assign and_1_out = A_rd & B_rs;  // AND_Gate and_1, 8 bits wide
  assign or_1_out = A_rd | B_rs;  // OR_Gate or_1, 8 bits wide
  Multiplexer #(.select(1), .width(8), .disabled("Z"), .enable("false")) multiplexer_2 (
    .in0(or_1_out), .in1(adder_1_out), .out(multiplexer_2_out), .sel(rs__rd));
  Adder #(.width(8)) adder_1 (.a(A_rd), .b(8'h1), .out(adder_1_out));  // open: cin, cout
  assign xor_1_out = A_rd ^ B_rs;  // XOR_Gate xor_1, 8 bits wide
  Adder #(.width(8)) adder_2 (.a(A_rd), .b(B_rs), .out(adder_2_out));  // open: cin, cout
  Subtractor #(.width(8)) subtractor_1 (.a(A_rd), .b(multiplexer_1_out), .out(subtractor_1_out));  // open: bin, bout
  Multiplier #(.width(8)) multiplier_1 (.a(A_rd), .b(B_rs), .out(multiplier_1_out));  // open: cin, cout
  Divider #(.width(8)) divider_1 (.a(A_rd), .b(B_rs), .out(divider_1_out));  // open: upper, rem
  ALU_2 alu_1 (.A(A_rd), .B(B_rs), .Out(alu_1_out));
  Multiplexer #(.select(3), .width(8), .disabled("Z"), .enable("false")) multiplexer_3 (
    .in0(and_1_out), .in1(multiplexer_2_out), .in2(xor_1_out), .in3(adder_2_out), .in4(subtractor_1_out),
    .in5(multiplier_1_out), .in6(divider_1_out), .in7(alu_1_out), .out({Negative, Result[6:0]}),
    .sel(Opcode[6:4]));
  Comparator #(.width(2), .mode("unsigned")) comparator_1 (
    .a(Opcode[1:0]), .b(Opcode[3:2]), .eq(rs__rd));  // open: gt, lt
  or or_2 (or_2_out, Result[0], Result[1], Result[2], Result[3], Result[4], Result[5], Result[6], Negative);
  not not_1 (Zero, or_2_out);

  assign Result[7] = Negative;

  // Notes on the sheet:
  //   8-bit ALU
  //   opcode
  //   if rs==rd
endmodule

module ALU_2 (
  input  [7:0] B,
  input  [7:0] A,
  output [7:0] Out
);

  wire [7:0] negator_1_out, shifter_1_out, shifter_2_out, shifter_3_out, shifter_4_out, undriven, undriven_2;

  Shifter #(.width(8), .shift("ll")) shifter_1 (.in(A), .\dist (B[2:0]), .out(shifter_1_out));
  Shifter #(.width(8), .shift("lr")) shifter_2 (.in(A), .\dist (B[2:0]), .out(shifter_2_out));
  Shifter #(.width(8), .shift("ar")) shifter_3 (.in(A), .\dist (B[2:0]), .out(shifter_3_out));
  Shifter #(.width(8), .shift("rl")) shifter_4 (.in(A), .\dist (B[2:0]), .out(shifter_4_out));
  Multiplexer #(.select(3), .width(8), .disabled("Z"), .enable("true")) multiplexer_1 (
    .in0(undriven), .in1(undriven_2), .in7(negator_1_out), .out(Out), .sel(B[2:0]), .en(B[7]));  // open: in2, in3, in4, in5, in6
  Negator #(.width(8)) negator_1 (.in(A), .out(negator_1_out));
  assign Out = B[3] ? shifter_1_out : 8'bz;  // Controlled_Buffer controlled_buffer_1
  assign Out = B[4] ? shifter_2_out : 8'bz;  // Controlled_Buffer controlled_buffer_2
  assign Out = B[5] ? shifter_3_out : 8'bz;  // Controlled_Buffer controlled_buffer_3
  assign Out = B[6] ? shifter_4_out : 8'bz;  // Controlled_Buffer controlled_buffer_4
  // Probe on Out
endmodule

module Port_Sel (
  input  [7:0] Addr,
  output RAM_sel,
  output IO_sel
);

  and and_1 (IO_sel, Addr[2], Addr[3], Addr[4], Addr[6], Addr[7], Addr[5]);
  not not_1 (RAM_sel, IO_sel);

  // Notes on the sheet:
  //   00-fb
  //   fc-ff
endmodule

module Port_S (
  input  [7:0] Address_Bus,
  input  [7:0] Port_s_Address,
  output Write_Enable
);

  wire [7:0] xnor_1_out;

  and and_1 (Write_Enable, xnor_1_out[7], xnor_1_out[7], xnor_1_out[6], xnor_1_out[5], xnor_1_out[4], xnor_1_out[3], xnor_1_out[2], xnor_1_out[1], xnor_1_out[0]);
  assign xnor_1_out = ~(Address_Bus ^ Port_s_Address);  // XNOR_Gate xnor_1, 8 bits wide
endmodule

module Port_range (
  input  [7:0] Address_Bus,
  input  [7:0] Range_LOW,
  input  [7:0] Range_HIGH,
  output Select
);

  wire comparator_1_eq, comparator_1_gt, comparator_2_eq, comparator_2_lt, or_1_out, or_2_out;

  or or_1 (or_1_out, comparator_1_eq, comparator_1_gt);
  Comparator #(.width(8), .mode("unsigned")) comparator_1 (
    .a(Address_Bus), .b(Range_LOW), .gt(comparator_1_gt), .eq(comparator_1_eq));  // open: lt
  and and_1 (Select, or_1_out, or_2_out);
  or or_2 (or_2_out, comparator_2_eq, comparator_2_lt);
  Comparator #(.width(8), .mode("unsigned")) comparator_2 (
    .a(Address_Bus), .b(Range_HIGH), .eq(comparator_2_eq), .lt(comparator_2_lt));  // open: gt
endmodule

module I_O (
  input  [3:0] in_1,
  input  [7:0] IN__0,
  input  [7:0] IN__1,
  input  [7:0] IN__2,
  input  [7:0] IN__3,
  input  [7:0] Addr,
  input  r_w,
  input  sel,
  input  [7:0] DATA_IN,
  input  CK,
  input  RT,
  output [7:0] D_BUS_OUT,
  output [7:0] OUT_0,
  output [7:0] OUT_1,
  output [7:0] OUT_2,
  output [7:0] OUT_3
);

  wire and_1_out, and_2_out, demultiplexer_1_out0, demultiplexer_1_out1, demultiplexer_1_out2,
       demultiplexer_1_out3;
  wire [7:0] register_1_q, register_2_q, register_3_q, register_4_q;

  and and_1 (and_1_out, r_w, sel);
  and and_2 (and_2_out, ~r_w, sel);  // AND_Gate
  Demultiplexer #(.select(2), .width(1), .tristate("false"), .disabled(0), .enable("false")) demultiplexer_1 (
    .out0(demultiplexer_1_out0), .out1(demultiplexer_1_out1), .out2(demultiplexer_1_out2),
    .out3(demultiplexer_1_out3), .in(and_1_out), .sel(Addr[1:0]));
  Register #(.width(8), .trigger("rising"), .Select("low")) register_1 (
    .D(IN__0), .Q(register_1_q), .clk(in_1[0]), .clr(RT));  // open: en
  Register #(.width(8), .trigger("rising"), .Select("low")) register_2 (
    .D(IN__1), .Q(register_2_q), .clk(in_1[1]), .clr(RT));  // open: en
  Register #(.width(8), .trigger("rising"), .Select("low")) register_3 (
    .D(IN__2), .Q(register_3_q), .clk(in_1[2]), .clr(RT));  // open: en
  Register #(.width(8), .trigger("rising"), .Select("low")) register_4 (
    .D(IN__3), .Q(register_4_q), .clk(in_1[3]), .clr(RT));  // open: en
  Register #(.width(8), .trigger("rising"), .Select("low")) register_5 (
    .D(DATA_IN), .en(demultiplexer_1_out0), .Q(OUT_0), .clk(CK), .clr(RT));
  Register #(.width(8), .trigger("rising"), .Select("low")) register_6 (
    .D(DATA_IN), .en(demultiplexer_1_out1), .Q(OUT_1), .clk(CK), .clr(RT));
  Register #(.width(8), .trigger("rising"), .Select("low")) register_7 (
    .D(DATA_IN), .en(demultiplexer_1_out2), .Q(OUT_2), .clk(CK), .clr(RT));
  Register #(.width(8), .trigger("rising"), .Select("low")) register_8 (
    .D(DATA_IN), .en(demultiplexer_1_out3), .Q(OUT_3), .clk(CK), .clr(RT));
  Multiplexer #(.select(2), .width(8), .disabled("Z"), .enable("true")) multiplexer_1 (
    .in0(register_1_q), .in1(register_2_q), .in2(register_3_q), .in3(register_4_q), .out(D_BUS_OUT),
    .sel(Addr[1:0]), .en(and_2_out));

  // Notes on the sheet:
  //   D_BUS_OUT: pull=down
  //   Addr: pull=down
  //   IN__1: pull=down
  //   IN__2: pull=down
  //   DATA_IN: pull=down
  //   IN__3: pull=down
  //   IN__0: pull=down
  //   读
endmodule

module IO (
  input  [3:0] in_1,
  input  [7:0] Addr,
  input  r_w,
  input  sel,
  input  [7:0] DATA_IN,
  input  [7:0] IN__0,
  input  [7:0] IN__1,
  input  [7:0] IN__2,
  input  [7:0] IN__3,
  input  CK,
  input  RT,
  output [7:0] D_BUS_OUT,
  output [7:0] OUT_0,
  output [7:0] OUT_1,
  output [7:0] OUT_2,
  output [7:0] OUT_3
);

  wire and_1_out, and_2_out, demultiplexer_1_out0, demultiplexer_1_out1, demultiplexer_1_out2,
       demultiplexer_1_out3;
  wire [7:0] controlled_buffer_1_out, or_1_out, or_2_out, or_3_out, or_4_out;

  assign controlled_buffer_1_out = r_w ? DATA_IN : 8'bz;  // Controlled_Buffer controlled_buffer_1
  assign or_1_out = IN__0 | controlled_buffer_1_out;  // OR_Gate or_1, 8 bits wide
  assign or_2_out = IN__1 | controlled_buffer_1_out;  // OR_Gate or_2, 8 bits wide
  assign or_3_out = IN__2 | controlled_buffer_1_out;  // OR_Gate or_3, 8 bits wide
  assign or_4_out = IN__3 | controlled_buffer_1_out;  // OR_Gate or_4, 8 bits wide
  and and_1 (and_1_out, ~r_w, sel);  // AND_Gate
  and and_2 (and_2_out, r_w, sel);
  Demultiplexer #(.select(2), .width(1), .tristate("false"), .disabled("Z"), .enable("false")) demultiplexer_1 (
    .out0(demultiplexer_1_out0), .out1(demultiplexer_1_out1), .out2(demultiplexer_1_out2),
    .out3(demultiplexer_1_out3), .in(and_2_out), .sel(Addr[1:0]));
  Register #(.width(8), .trigger("rising"), .Select("low")) register_1 (
    .D(or_1_out), .en(demultiplexer_1_out0), .Q(OUT_0), .clk(CK), .clr(RT));
  Register #(.width(8), .trigger("rising"), .Select("low")) register_2 (
    .D(or_2_out), .en(demultiplexer_1_out1), .Q(OUT_1), .clk(CK), .clr(RT));
  Register #(.width(8), .trigger("rising"), .Select("low")) register_3 (
    .D(or_3_out), .en(demultiplexer_1_out2), .Q(OUT_2), .clk(CK), .clr(RT));
  Register #(.width(8), .trigger("rising"), .Select("low")) register_4 (
    .D(or_4_out), .en(demultiplexer_1_out3), .Q(OUT_3), .clk(CK), .clr(RT));
  Multiplexer #(.select(2), .width(8), .disabled("Z"), .enable("true")) multiplexer_1 (
    .in0(OUT_0), .in1(OUT_1), .in2(OUT_2), .in3(OUT_3), .out(D_BUS_OUT), .sel(Addr[1:0]), .en(and_1_out));

  // Notes on the sheet:
  //   IN__2: pull=down
  //   DATA_IN: pull=down
  //   D_BUS_OUT: pull=down
  //   IN__0: pull=down
  //   Addr: pull=down
  //   IN__3: pull=down
  //   IN__1: pull=down
  //   读
  //   写
endmodule
